# Fritzing sketch breadboard-v0 (saved by Fritzing 0.9.2b)
breadboards: 1

parts:
  TRS1 = Audio Jack (TRS) 3.5mm [package="4Ucon 08780 [THT]"]
  TRS2 = Audio Jack (TRS) 3.5mm [package="4Ucon 08780 [THT]"]
  TRS3 = Audio Jack (TRS) 3.5mm [package="4Ucon 08780 [THT]"]
  U1 = SWITCH-SPST-2 [package=switch-spst-vertical]
  VCC1 = Battery

nets:
  N1: TRS1.Sleeve, TRS2.Sleeve, TRS3.Sleeve, VCC1.-
  N2: TRS1.Ring, TRS2.Ring, TRS3.Ring, U1.O
  N3: TRS1.Tip, TRS2.Tip
  N4: U1.P, VCC1.+

notes:
  connect to RedBearLab Blend A0, A1, A2
  connect to RedBearLab 3.3V
  connect to RedBearLab GND
